# Fritzing sketch Planta_IoT (saved by Fritzing 0.9.3b)

parts:
  U1 = NodeMCU V1.0
  Componente1 = FC-28 Soil Hygrometer Module
  Componente2 = FC-28 Soil Hygrometer Module - Probe

nets:
  VIN: U1.Vin, Componente1.VCC
  GND: U1.GND, Componente1.GND
  N1: U1.A0, Componente1.AO
  N2: Componente1.POS, Componente2.POS
  N3: Componente1.NEG, Componente2.NEG

custom parts:
  NodeMCU V1.0: ESP8266 based NodeMCU
  FC-28 Soil Hygrometer Module: The FC-28 is a soil hygrometer module that uses the Texas Instruments LM393 comparator chip to provide an analog measurement of soil humidity. The digital output is high when soil moisture is over a certain threshold, as determined by adjusting the potentiometer.
  FC-28 Soil Hygrometer Module - Probe: The FC-28 is a soil hygrometer module that uses the Texas Instruments LM393 comparator chip to provide an analog measurement of soil humidity.
